# Fritzing sketch wiring (saved by Fritzing 0.7.4b)
breadboards: 2

parts:
  18f1 = DIP - 40 pins [package="DIP (Dual Inline) [THT]"]
  R2 = Rotary Potentiometer (Small) [maximum_resistance=50kΩ]
  GLCD_128x1 = 128 x 64 Graphic LCD
  R1 = Resistor [tolerance=±5% resistance=10k package=THT]
  C1 = Tantalum Capacitor [capacitance=22pF package="100 mil [THT, tantalum]"]
  C2 = Tantalum Capacitor [capacitance=22pF package="100 mil [THT, tantalum]"]
  XTAL1 = Crystal [frequency="4 MHz" package=THT]
  S1 = Pushbutton [package="[THT]"]
  R3 = Resistor [tolerance=±5% resistance=1k package=THT]
  S2 = Pushbutton [package="[THT]"]
  R4 = Resistor [tolerance=±5% resistance=1k package=THT]
  S3 = Pushbutton [package="[THT]"]
  R5 = Resistor [tolerance=±5% resistance=1k package=THT]
  S5 = Pushbutton [package="[THT]"]
  R7 = Resistor [tolerance=±5% resistance=1k package=THT]
  S6 = Pushbutton [package="[THT]"]
  R8 = Resistor [tolerance=±5% resistance=1k package=THT]
  S7 = Pushbutton [package="[THT]"]
  R9 = Resistor [tolerance=±5% resistance=1k package=THT]
  S8 = Pushbutton [package="[THT]"]
  R10 = Resistor [tolerance=±5% resistance=1k package=THT]

nets:
  N1: 18f1.MCLR/VPP/RE3, R1.Pin_1
  N2: 18f1.RA0/AN0, GLCD_128x1.17_RST
  N3: 18f1.RA1/AN1, GLCD_128x1.16_CS2
  N4: 18f1.RA2/AN2/VREF-/CVREF, GLCD_128x1.15_CS1
  N5: 18f1.RA3/AN3/VREF+, GLCD_128x1.6_Enable
  N6: 18f1.RA4/T0CKI/C1OUT/RCV, GLCD_128x1.5_R/W
  N7: 18f1.RA5/AN4/SS/HLVDIN/C2OUT, GLCD_128x1.4_D/I
  N8: 18f1.VDD, R2.leg2, GLCD_128x1.2_Vdd, GLCD_128x1.19_A(+), R1.Pin_0, S1.Pin_3, S1.Pin_4, S2.Pin_3, S2.Pin_4, S3.Pin_3, S3.Pin_4, S5.Pin_3, S5.Pin_4, S6.Pin_3, S6.Pin_4, S7.Pin_3, S7.Pin_4, S8.Pin_3, S8.Pin_4
  N9: 18f1.VSS, GLCD_128x1.1_Vss, GLCD_128x1.20_K(-), C1.-, C2.-, R3.Pin_1, R4.Pin_1, R5.Pin_1, R7.Pin_1, R8.Pin_1, R9.Pin_1, R10.Pin_1
  N10: 18f1.OSC1/CLKI, C1.+, XTAL1.pin_1
  N11: 18f1.OSC2/CLKO/RA6, C2.+, XTAL1.pin_0
  N12: 18f1.RD5/SPP5/P1B#18, 18f1.RB0/AN12/INT0/FLT0/SDI/SDA, GLCD_128x1.14_DB7, S8.Pin_1, S8.Pin_2, R10.Pin_0
  N13: 18f1.RD1/SPP1, 18f1.RB1/AN10/INT1/SCK/SCL, GLCD_128x1.13_DB6, S7.Pin_1, S7.Pin_2, R9.Pin_0
  N14: 18f1.RD2/SPP2, 18f1.RB2/AN8/INT2/VMO, GLCD_128x1.12_DB5, S6.Pin_1, S6.Pin_2, R8.Pin_0
  N15: 18f1.RD3/SPP3, 18f1.RB3/AN9/CCP2(1)/VPO, GLCD_128x1.11_DB4, S5.Pin_1, S5.Pin_2, R7.Pin_0
  N16: 18f1.RD4/SPP4, 18f1.RB4/AN11/KBI0/CSSPP, GLCD_128x1.10_DB3
  N17: 18f1.RD5/SPP5/P1B#27, 18f1.RB5/KBI1/PGM, GLCD_128x1.9_BD2, S3.Pin_1, S3.Pin_2, R5.Pin_0
  N18: 18f1.RD6/SPP6/P1C, 18f1.RB6/KBI2/PGC, GLCD_128x1.8_DB1, S2.Pin_1, S2.Pin_2, R4.Pin_0
  N19: 18f1.RD7/SPP7/P1D, 18f1.RB7/KBI3/PGD, GLCD_128x1.7_DB0, S1.Pin_1, S1.Pin_2, R3.Pin_0
  N20: R2.leg1, GLCD_128x1.3_Vo
  N21: R2.wiper, GLCD_128x1.18_Vout

notes:
  10k pin 1 to vcc
  50k var res
  (contrast)
  1k to the gnd
  2X22Pf and 4MHz OCS

custom parts:
  DIP - 40 pins: A DIP stand-in part for whatever IC you want. With 40 pins on a 300 mil dual inline package (DIP) footprint.
